# Fritzing sketch HeadtrackerBoard (saved by Fritzing 0.9.4)
circuit board: 1.80451cm x 3.67512cm
breadboards: 1

parts:
  Arduino = 9-DOF Absolute Orientation IMU Fusion Breakout - BNO055
  BNO055 = SparkFun Pro Micro

nets:
  N1: Arduino.5.0V, BNO055.VCC
  GND: Arduino.GND, BNO055.GND
  N2: Arduino.SDA_5V, BNO055.2
  N3: Arduino.SCL_5V, BNO055.3

custom parts:
  9-DOF Absolute Orientation IMU Fusion Breakout - BNO055: A MEMS accelerometer, magnetometer and gyroscope on a single die with a high speed ARM Cortex-M0 based processor to digest all the sensor data, abstract the sensor fusion and real time requirements away, and spit out data you can use in quaternions, Euler angles or vectors.
  SparkFun Pro Micro: The Pro Micro is similar to the Pro Mini except with an ATmega32U4 on board. The USB transceiver inside the 32U4 allows us to add USB connectivity on-board and do away with bulky external USB interface. Based on: https://github.com/unorthodox-engineers/unorthodox-arduino/blob/master/Unorthodox/fritzing/parts/Pro%20Micro.fzpz
